// Logisim project LogisimExample.circ as structural Verilog: 2 circuits, main circuit main
module main (
  input  in_1,
  output out_2
);

  not not_1 (out_2, in_1);
  sth sth_1 ();  // open: in_1, in_2, O
  // LogisimExampleLib_main main_1: pin names not known
endmodule

module sth (
  input  in_1,
  input  in_2,
  output O
);

  and and_1 (O, in_1, in_2);
endmodule
