// Logisim project LogisimExampleLib.circ as structural Verilog: 1 circuit, main circuit main
module main (
  input  in_1
);

  // Probe on nothing
  Pull_Resistor pull_resistor_1 ();  // open: node
  Clock clock_1 ();  // open: out
  // NOT_Gate not_1 is placed but not wired
  // Buffer buffer_1 is placed but not wired
  // AND_Gate and_1 is placed but not wired
  Transistor transistor_1 ();  // open: in, out, gate
  // Transmission_Gate transmission_1: pin names not known
  Bit_Extender bit_extender_1 ();  // open: in, out
endmodule
